// Logisim project SymulatorProfesora.circ as structural Verilog: 1 circuit, main circuit main
module main (
  input  in_1,
  input  in_2,
  input  send,
  input  send_2,
  input  send_3,
  input  send_4,
  input  send_5,
  input  send_6
);

  wire clock_1_out, clock_2_out, comparator_1_eq, comparator_2_eq, main_1_output, main_4_p3, main_4_p5,
       main_5_p3, main_6_p3, main_7_p3, main_8_p3, main_15_done, or_1_out, or_3_out;
  wire [4:0] adder_1_out, counter_1_q, counter_2_q, register_1_q;
  wire [6:0] keyboard_1_data, main_2_output;
  wire [31:0] main_3_output, main_4_p4, main_5_p4, main_6_p4, main_7_p4, main_8_p4, main_15_out_4,
       main_15_out_5, main_15_out_6, main_15_out_7, main_15_out_8, main_15_out_9, main_15_out_10,
       main_15_out_11, main_15_out_12, main_15_out_13, main_15_out_14, main_15_out_15, main_15_out_16,
       main_15_out_17, main_15_out_18, main_15_out_19, main_15_out_20, main_15_out_21, main_15_out_22,
       main_15_out_23, main_15_out_24, main_15_out_25, main_15_out_26, main_15_out_27, main_15_out_28,
       main_15_out_29, main_15_out_30, main_15_out_31, main_15_out_32, main_15_out_33, main_15_out_34,
       main_15_out_35, or_2_out, rom_1_data, rom_2_data, rom_3_data, rom_4_data, rom_5_data, rom_6_data,
       rom_7_data;

  Keyboard #(.buflen(1)) keyboard_1 (.clk(clock_1_out), .re(1'b1), .data(keyboard_1_data));  // open: clr, avail
  Comparator #(.width(7), .mode("unsigned")) comparator_1 (
    .a(keyboard_1_data), .b(7'b1100100), .eq(comparator_1_eq));  // open: gt, lt
  Comparator #(.width(7), .mode("unsigned")) comparator_2 (
    .a(keyboard_1_data), .b(7'b1100001), .eq(comparator_2_eq));  // open: gt, lt
  Counter #(.width(5), .max('h1b), .ongoal("stay")) counter_1 (
    .load(comparator_1_eq), .Q(counter_1_q), .clk(or_1_out));  // open: D, count, carry, clr
  or or_1 (or_1_out, comparator_1_eq, comparator_2_eq);
  Counter #(.width(5), .max('h1f)) counter_2 (.Q(counter_2_q), .clk(clock_1_out));  // open: load, D, count, carry, clr
  Clock clock_1 (.out(clock_1_out));
  Clock clock_2 (.out(clock_2_out));
  Register #(.width(5)) register_1 (.D(counter_1_q), .Q(register_1_q), .clk(main_15_done));  // open: en, clr
  Adder #(.width(5)) adder_1 (.a(register_1_q), .b(counter_2_q), .out(adder_1_out));  // open: cin, cout
  single_pulse_generator_main main_1 (.trigger(in_1), .\output (main_1_output), .clock(clock_2_out));
  ROM #(.addrWidth(5), .dataWidth(32)) rom_1 (.addr(adder_1_out), .data(rom_1_data));  // open: sel
  ROM_message_spitter_main main_2 (
    .clock(clock_2_out), .\output (main_2_output), .trigger(main_1_output), .reset(in_2));
  ROM #(.addrWidth(5), .dataWidth(32)) rom_2 (.addr(counter_2_q), .data(rom_2_data));  // open: sel
  ROM #(.addrWidth(5), .dataWidth(32)) rom_3 (.addr(counter_2_q), .data(rom_3_data));  // open: sel
  ROM #(.addrWidth(5), .dataWidth(32)) rom_4 (.addr(counter_2_q), .data(rom_4_data));  // open: sel
  ROM #(.addrWidth(5), .dataWidth(32)) rom_5 (.addr(counter_2_q), .data(rom_5_data));  // open: sel
  ROM #(.addrWidth(5), .dataWidth(32)) rom_6 (.addr(counter_2_q), .data(rom_6_data));  // open: sel
  ROM #(.addrWidth(5), .dataWidth(32)) rom_7 (.addr(counter_2_q), .data(rom_7_data));  // open: sel
  TTY #(.rows(1), .cols(110)) tty_1 (.data(main_2_output), .clk(clock_2_out), .clr(main_1_output));  // open: we
  student_drop_main main_3 (
    .\input (rom_2_data), .send(send), .\output (main_3_output), .catch(main_4_p5));  // open: clk
  // student_drop_main main_4: pin names not known; wires that end beside it: rom_3_data, send_2, main_4_p3, main_4_p4, main_4_p5
  // student_drop_main main_5: pin names not known; wires that end beside it: rom_4_data, send_3, main_5_p3, main_5_p4, main_4_p3
  // student_drop_main main_6: pin names not known; wires that end beside it: rom_5_data, send_4, main_6_p3, main_6_p4, main_5_p3
  // student_drop_main main_7: pin names not known; wires that end beside it: rom_6_data, send_5, main_7_p3, main_7_p4, main_6_p3
  // student_drop_main main_8: pin names not known; wires that end beside it: rom_7_data, send_6, main_8_p3, main_8_p4, main_7_p3
  student_catcher_main main_9 (.student(main_3_output), .catch(main_4_p5), .profesor(rom_1_data));
  student_catcher_main main_10 (.student(main_4_p4), .catch(main_4_p3), .profesor(rom_1_data));
  student_catcher_main main_11 (.student(main_5_p4), .catch(main_5_p3), .profesor(rom_1_data));
  student_catcher_main main_12 (.student(main_6_p4), .catch(main_6_p3), .profesor(rom_1_data));
  student_catcher_main main_13 (.student(main_7_p4), .catch(main_7_p3), .profesor(rom_1_data));
  student_catcher_main main_14 (.student(main_8_p4), .catch(main_8_p3), .profesor(rom_1_data));
  Counter counter_3 (.clk(or_3_out));  // open: load, D, count, Q, carry, clr
  assign or_2_out = main_3_output | main_4_p4 | main_5_p4 | rom_1_data | main_6_p4 | main_7_p4 | main_8_p4;  // OR_Gate or_2, 32 bits wide
  or or_3 (or_3_out, main_8_p3, main_7_p3, main_6_p3, main_5_p3, main_4_p3, main_4_p5);
  display_buffer_main main_15 (
    .Address(or_2_out), .Select(counter_2_q), .out_4(main_15_out_4), .out_5(main_15_out_5),
    .out_6(main_15_out_6), .out_7(main_15_out_7), .out_8(main_15_out_8), .out_9(main_15_out_9),
    .out_10(main_15_out_10), .out_11(main_15_out_11), .out_12(main_15_out_12), .out_13(main_15_out_13),
    .out_14(main_15_out_14), .out_15(main_15_out_15), .out_16(main_15_out_16), .out_17(main_15_out_17),
    .out_18(main_15_out_18), .out_19(main_15_out_19), .out_20(main_15_out_20), .out_21(main_15_out_21),
    .out_22(main_15_out_22), .out_23(main_15_out_23), .out_24(main_15_out_24), .out_25(main_15_out_25),
    .out_26(main_15_out_26), .out_27(main_15_out_27), .out_28(main_15_out_28), .out_29(main_15_out_29),
    .out_30(main_15_out_30), .out_31(main_15_out_31), .out_32(main_15_out_32), .out_33(main_15_out_33),
    .out_34(main_15_out_34), .out_35(main_15_out_35), .Done(main_15_done));
  DotMatrix #(.matrixcols(32), .matrixrows(32)) dotmatrix_1 (
    .col0(main_15_out_4), .col1(main_15_out_5), .col2(main_15_out_6), .col3(main_15_out_7),
    .col4(main_15_out_8), .col5(main_15_out_9), .col6(main_15_out_10), .col7(main_15_out_11),
    .col8(main_15_out_12), .col9(main_15_out_13), .col10(main_15_out_14), .col11(main_15_out_15),
    .col12(main_15_out_16), .col13(main_15_out_17), .col14(main_15_out_18), .col15(main_15_out_19),
    .col16(main_15_out_20), .col17(main_15_out_21), .col18(main_15_out_22), .col19(main_15_out_23),
    .col20(main_15_out_24), .col21(main_15_out_25), .col22(main_15_out_26), .col23(main_15_out_27),
    .col24(main_15_out_28), .col25(main_15_out_29), .col26(main_15_out_30), .col27(main_15_out_31),
    .col28(main_15_out_32), .col29(main_15_out_33), .col30(main_15_out_34), .col31(main_15_out_35));

  // Notes on the sheet:
  //   keyboard
  //   a
  //   d
  //   Zegar:szybko
  //   A6
  //   A5
  //   A4
  //   A3
  //   A2
  //   A1
  //   contents of rom_1 (hex, n*v repeats v):
  //   27*0 4 7 e 7 4
  //   profesor
  //   contents of rom_2 (hex, n*v repeats v):
  //   0 50000000 e0000000 50000000
  //   contents of rom_3 (hex, n*v repeats v):
  //   6*0 50000000 e0000000 50000000
  //   contents of rom_4 (hex, n*v repeats v):
  //   12*0 50000000 e0000000 50000000
  //   contents of rom_5 (hex, n*v repeats v):
  //   17*0 50000000 e0000000 50000000
  //   contents of rom_6 (hex, n*v repeats v):
  //   23*0 50000000 e0000000 50000000
  //   contents of rom_7 (hex, n*v repeats v):
  //   28*0 50000000 e0000000 50000000
endmodule
